// Logisim project Version_05_Assignment_CNA.circ as structural Verilog: 1 circuit, main circuit main
module main (
  input  C1_3,
  input  C1_2,
  input  C1_1,
  input  [2:0] N,
  input  Start,
  input  C2_1,
  input  C2_2,
  input  [2:0] in_8,
  input  C2_3
);

  wire and_1_out, and_2_out, and_3_out, and_4_out, and_5_out, and_6_out, and_7_out, and_8_out, and_9_out,
       and_10_out, and_11_out, and_12_out, and_13_out, and_14_out, and_15_out, and_16_out, and_17_out,
       and_18_out, and_19_out, and_20_out, and_21_out, and_22_out, and_23_out, and_24_out, button_1_out,
       C1_0_out, C1_1_out, C1_4_out, C1_5_out, C1_6_out, C1_7_out, C2_0_2_out, C2_0_out, C2_1_2_out,
       C2_1_out, C2_2_2_out, C2_2_out, C2_3_2_out, C2_3_out, C2_4_2_out, C2_4_out, C2_5_2_out, C2_5_out,
       C2_6_out, C2_7_out, C2__1_out, C__2_out, C__3_out, comparator_1_eq, comparator_2_eq, comparator_3_eq,
       LOCK_out, Lockout_Block_out, N_000_out, not_1_out, not_2_out, not_3_out, not_4_out, not_5_out,
       not_6_out, not_7_out, not_8_out, not_9_out, not_10_out, or_1_out, or_2_out, or_3_out, or_4_out,
       or_5_out, or_6_out, or_7_out, Reset_out, Start_Block_2_out, Start_Block_3_out, Start_Block_out;
  wire [2:0] counter_1_q, counter_2_q;

  not not_1 (not_1_out, C1_1);
  Button button_1 (.out(button_1_out));
  not not_2 (not_2_out, C2_1);
  not not_3 (not_3_out, C1_3);
  not not_4 (not_4_out, C1_2);
  not not_5 (not_5_out, C2_2);
  not not_6 (not_6_out, C2_3);
  and and_1 (and_1_out, C1_3, C1_2);
  and and_2 (and_2_out, not_3_out, C1_2);
  and and_3 (and_3_out, C1_3, not_4_out);
  and and_4 (and_4_out, not_3_out, not_4_out);
  and and_5 (and_5_out, C1_3, C1_2);
  and and_6 (and_6_out, not_3_out, C1_2);
  and and_7 (and_7_out, C1_3, not_4_out);
  and and_8 (and_8_out, not_3_out, not_4_out);
  and and_9 (and_9_out, not_5_out, not_6_out);
  and and_10 (and_10_out, not_5_out, C2_3);
  and and_11 (and_11_out, C2_2, not_6_out);
  and and_12 (and_12_out, C2_2, C2_3);
  and and_13 (and_13_out, not_5_out, not_6_out);
  and and_14 (and_14_out, not_5_out, C2_3);
  and and_15 (and_15_out, C2_2, not_6_out);
  and and_16 (and_16_out, C2_2, C2_3);
  and C1_7 (C1_7_out, and_1_out, C1_1);
  and C1_6 (C1_6_out, and_2_out, C1_1);
  and C1_5 (C1_5_out, and_3_out, C1_1);
  and C1_4 (C1_4_out, and_4_out, C1_1);
  and C__3 (C__3_out, and_5_out, not_1_out);
  and C__2 (C__2_out, and_6_out, not_1_out);
  and u_C1_1 (C1_1_out, and_7_out, not_1_out);
  and C1_0 (C1_0_out, and_8_out, not_1_out);
  or C2__1 (C2__1_out, C2_0_out, C2_0_2_out);
  and C2_0 (C2_0_out, not_2_out, and_9_out);
  and u_C2_1 (C2_1_out, not_2_out, and_10_out);
  and u_C2_2 (C2_2_out, not_2_out, and_11_out);
  and u_C2_3 (C2_3_out, not_2_out, and_12_out);
  and C2_4 (C2_4_out, C2_1, and_13_out);
  and C2_5 (C2_5_out, C2_1, and_14_out);
  and C2_6 (C2_6_out, C2_1, and_15_out);
  and C2_7 (C2_7_out, C2_1, and_16_out);
  or C2_0_2 (C2_0_2_out, C2_1_out, C2_1_2_out);
  or C2_1_2 (C2_1_2_out, C2_2_out, C2_2_2_out);
  or C2_2_2 (C2_2_2_out, C2_3_out, C2_3_2_out);
  or C2_3_2 (C2_3_2_out, C2_4_out, C2_4_2_out);
  or C2_4_2 (C2_4_2_out, C2_5_out, C2_5_2_out);
  or C2_5_2 (C2_5_2_out, C2_6_out, C2_7_out);
  and and_17 (and_17_out, C1_7_out, C2__1_out);
  and and_18 (and_18_out, C1_6_out, C2_0_2_out);
  and and_19 (and_19_out, C1_5_out, C2_1_2_out);
  and and_20 (and_20_out, C1_4_out, C2_2_2_out);
  and and_21 (and_21_out, C__3_out, C2_3_2_out);
  and and_22 (and_22_out, C__2_out, C2_4_2_out);
  and and_23 (and_23_out, C1_1_out, C2_5_2_out);
  and and_24 (and_24_out, C1_0_out, C2_7_out);
  or or_1 (or_1_out, and_17_out, and_18_out);
  or or_2 (or_2_out, and_19_out, and_20_out);
  or or_3 (or_3_out, and_21_out, and_22_out);
  or or_4 (or_4_out, and_23_out, and_24_out);
  Comparator #(.width(3)) comparator_1 (.a(N), .b(in_8), .eq(comparator_1_eq));  // open: gt, lt
  or or_5 (or_5_out, or_1_out, or_2_out);
  or or_6 (or_6_out, or_3_out, or_4_out);
  and N_000 (N_000_out, Start, not_7_out);
  not not_7 (not_7_out, comparator_1_eq);
  or or_7 (or_7_out, or_5_out, or_6_out);
  LED Winner_for_round (.in(not_9_out));
  and Reset (Reset_out, button_1_out, not_8_out);
  not not_8 (not_8_out, N_000_out);
  not not_9 (not_9_out, or_7_out);
  and Start_Block (Start_Block_out, Lockout_Block_out, N_000_out);
  and Lockout_Block (Lockout_Block_out, button_1_out, not_10_out);
  Counter #(.width(3), .max('h7), .ongoal("stay")) counter_1 (
    .load(or_7_out), .Q(counter_1_q), .clk(Start_Block_out), .clr(Reset_out));  // open: D, count, carry
  Counter #(.width(3), .max('h7), .ongoal("stay")) counter_2 (
    .load(not_9_out), .Q(counter_2_q), .clk(Start_Block_out), .clr(Reset_out));  // open: D, count, carry
  Comparator #(.width(3)) comparator_2 (.a(counter_1_q), .b(N), .eq(comparator_2_eq));  // open: gt, lt
  Comparator #(.width(3)) comparator_3 (.a(counter_2_q), .b(N), .eq(comparator_3_eq));  // open: gt, lt
  not not_10 (not_10_out, LOCK_out);
  and Start_Block_2 (Start_Block_2_out, comparator_2_eq, N_000_out);
  and Start_Block_3 (Start_Block_3_out, comparator_3_eq, N_000_out);
  or LOCK (LOCK_out, Start_Block_3_out, Start_Block_2_out);
  LED OVERALL_WINNER (.in(Start_Block_2_out));
  LED OVERALL_LOSER (.in(Start_Block_3_out));

  // Notes on the sheet:
  //   If start is off Reset if on play till N
  //   C2>6
  //   Doesn't Allow start if N=000
  //   Counter For Wins
  //   Counter For Losses
  //   Compairs Win/Loss to N
endmodule
