// Logisim project s5084150_Carl_Humphries_Logic_Circuit.circ as structural Verilog: 5 circuits, main circuit main
module main (
  input  C1_3,
  input  C1_2,
  input  C1_1,
  input  C2_1,
  input  C2_2,
  input  C2_3,
  input  [2:0] CONSTANT_000,
  input  [2:0] N,
  input  Start
);

  wire Clock_Button_out, comparator_1_eq, comparator_2_eq, comparator_3_eq, LOCK_out, Lockout_Block_out,
       N_000_out, not_1_out, not_2_out, not_3_out, not_4_out, part_a_1_winner, Reset_out, Start_Block_2_out,
       Start_Block_3_out, Start_Block_out;
  wire [2:0] counter_1_q, counter_2_q;

  Button Clock_Button (.out(Clock_Button_out));
  not not_1 (not_1_out, comparator_1_eq);
  Comparator #(.width(3)) comparator_1 (.a(CONSTANT_000), .b(N), .eq(comparator_1_eq));  // open: gt, lt
  and N_000 (N_000_out, Start, not_1_out);
  Part_A part_a_1 (
    .C1_3(C1_3), .C1_2(C1_2), .C1_1(C1_1), .C2_1(C2_1), .C2_2(C2_2), .C2_3(C2_3), .Winner(part_a_1_winner));
  and Reset (Reset_out, Clock_Button_out, not_2_out);
  not not_2 (not_2_out, N_000_out);
  not not_3 (not_3_out, part_a_1_winner);
  and Start_Block (Start_Block_out, Lockout_Block_out, N_000_out);
  and Lockout_Block (Lockout_Block_out, Clock_Button_out, not_4_out);
  Counter #(.width(3), .max('h7), .ongoal("stay")) counter_1 (
    .load(not_3_out), .Q(counter_1_q), .clk(Start_Block_out), .clr(Reset_out));  // open: D, count, carry
  Counter #(.width(3), .max('h7), .ongoal("stay")) counter_2 (
    .load(part_a_1_winner), .Q(counter_2_q), .clk(Start_Block_out), .clr(Reset_out));  // open: D, count, carry
  Comparator #(.width(3)) comparator_2 (.a(counter_1_q), .b(N), .eq(comparator_2_eq));  // open: gt, lt
  Comparator #(.width(3)) comparator_3 (.a(counter_2_q), .b(N), .eq(comparator_3_eq));  // open: gt, lt
  and Start_Block_2 (Start_Block_2_out, comparator_2_eq, N_000_out);
  and Start_Block_3 (Start_Block_3_out, comparator_3_eq, N_000_out);
  or LOCK (LOCK_out, Start_Block_3_out, Start_Block_2_out);
  not not_4 (not_4_out, LOCK_out);
  LED OVERALL_WINNER (.in(Start_Block_2_out));
  LED OVERALL_LOSER (.in(Start_Block_3_out));

  // Notes on the sheet:
  //   Main Part A and B 
  //   Name: Carl Humphries
  //   Student Number: S5084150
  //   Doesn't Allow start if N=000
  //   If start is off Reset if on play till N
  //   Part A
  //   Win=True
  //   It compairs N to 000 before allowing to start and if Start is False then the clock resets the circuit
  //   This circuit uses counters to count the win or loss and uses sets of blockers(AND gates) to allow this if certain cirumstances
  //   Are True From there it compair with the inputed N and will lock using the output once either the wins or losses are equal to n
  //   Counter For Wins
  //   Counter For Losses
  //   Compairs Win/Loss to N
endmodule

module _3_8_Decoder_7_Top_0_Bottom (
  input  C3,
  input  C2,
  input  C1,
  output _7,
  output _6,
  output _5,
  output _4,
  output _3,
  output _2,
  output _1,
  output _0
);

  wire and_1_out, and_2_out, and_3_out, and_4_out, and_5_out, and_6_out, and_7_out, and_8_out, not_1_out,
       not_2_out, not_3_out;

  not not_1 (not_1_out, C1);
  not not_2 (not_2_out, C3);
  not not_3 (not_3_out, C2);
  and and_1 (and_1_out, C3, C2);
  and and_2 (and_2_out, not_2_out, C2);
  and and_3 (and_3_out, C3, not_3_out);
  and and_4 (and_4_out, not_2_out, not_3_out);
  and and_5 (and_5_out, C3, C2);
  and and_6 (and_6_out, not_2_out, C2);
  and and_7 (and_7_out, C3, not_3_out);
  and and_8 (and_8_out, not_2_out, not_3_out);
  and and_9 (_7, and_1_out, C1);
  and and_10 (_6, and_2_out, C1);
  and and_11 (_5, and_3_out, C1);
  and and_12 (_4, and_4_out, C1);
  and and_13 (_3, and_5_out, not_1_out);
  and and_14 (_2, and_6_out, not_1_out);
  and and_15 (_1, and_7_out, not_1_out);
  and and_16 (_0, and_8_out, not_1_out);

  // Notes on the sheet:
  //   3:8 Decoder  
  //   Using Three inputs
  //   Name: Carl Humphries
  //   Student Number: S5084150
  //   The decoder turns it into one unique output
  //   It is similar to representing an octal digit    
  //   Details on how it works are in the report.
endmodule

module Card_Logic (
  input  C1_7,
  input  C1_6,
  input  C1_5,
  input  C1_4,
  input  C1_3,
  input  C1_2,
  input  C1_1,
  input  C1_0,
  input  C2_0,
  input  C2_1,
  input  C2_2,
  input  C2_3,
  input  C2_4,
  input  C2_5,
  input  C2_6,
  input  C2_7,
  output C1_C2_7_True
);

  wire and_1_out, and_2_out, and_3_out, and_4_out, and_5_out, and_6_out, and_7_out, and_8_out, C2_0_out,
       C2_1_out, C2_2_out, C2_3_out, C2_4_out, C2_5_out, C2__1_out, or_1_out, or_2_out, or_3_out, or_4_out,
       or_5_out, or_6_out, or_7_out;

  or C2__1 (C2__1_out, C2_0, C2_0_out);
  or u_C2_0 (C2_0_out, C2_1, C2_1_out);
  or u_C2_1 (C2_1_out, C2_2, C2_2_out);
  or u_C2_2 (C2_2_out, C2_3, C2_3_out);
  or u_C2_3 (C2_3_out, C2_4, C2_4_out);
  or u_C2_4 (C2_4_out, C2_5, C2_5_out);
  or u_C2_5 (C2_5_out, C2_6, C2_7);
  and and_1 (and_1_out, C1_7, C2__1_out);
  and and_2 (and_2_out, C1_6, C2_0_out);
  and and_3 (and_3_out, C1_5, C2_1_out);
  and and_4 (and_4_out, C1_4, C2_2_out);
  and and_5 (and_5_out, C1_3, C2_3_out);
  and and_6 (and_6_out, C1_2, C2_4_out);
  and and_7 (and_7_out, C1_1, C2_5_out);
  and and_8 (and_8_out, C1_0, C2_7);
  or or_1 (or_1_out, and_1_out, and_2_out);
  or or_2 (or_2_out, and_3_out, and_4_out);
  or or_3 (or_3_out, and_5_out, and_6_out);
  or or_4 (or_4_out, and_7_out, and_8_out);
  or or_5 (or_5_out, or_1_out, or_2_out);
  or or_6 (or_6_out, or_3_out, or_4_out);
  or or_7 (or_7_out, or_5_out, or_6_out);
  not not_1 (C1_C2_7_True, or_7_out);

  // Notes on the sheet:
  //   Card Logic  
  //   Name: Carl Humphries
  //   Student Number: S5084150
  //   Using Input of numbers from the decoders
  //   Details on how it works are in the report.
  //   It calculates C2 into greater than all numbers before it lighting up all the lines before it.
  //   It calculates if the person has busted and sends that signal through but if they haven't they have won
  //   C2>6
  //   C1=7
  //   C2>-1
  //   C1=6
  //   C2>0
  //   C1=5
  //   C2>1
  //   C1=4
  //   C2>2
  //   C1=3
  //   C2>3
  //   C1=2
  //   C2>4
  //   C1=1
  //   C2>5
  //   C1=0
  //   C2>6
endmodule

module _3_8_Decoder_0_Top_7_Bottom (
  input  C1,
  input  C2,
  input  C3,
  output _0,
  output _1,
  output _2,
  output _3,
  output _4,
  output _5,
  output _6,
  output _7
);

  wire and_1_out, and_2_out, and_3_out, and_4_out, and_5_out, and_6_out, and_7_out, and_8_out, not_1_out,
       not_2_out, not_3_out;

  not not_1 (not_1_out, C1);
  not not_2 (not_2_out, C2);
  not not_3 (not_3_out, C3);
  and and_1 (and_1_out, not_2_out, not_3_out);
  and and_2 (and_2_out, not_2_out, C3);
  and and_3 (and_3_out, C2, not_3_out);
  and and_4 (and_4_out, C2, C3);
  and and_5 (and_5_out, not_2_out, not_3_out);
  and and_6 (and_6_out, not_2_out, C3);
  and and_7 (and_7_out, C2, not_3_out);
  and and_8 (and_8_out, C2, C3);
  and and_9 (_0, not_1_out, and_1_out);
  and and_10 (_1, not_1_out, and_2_out);
  and and_11 (_2, not_1_out, and_3_out);
  and and_12 (_3, not_1_out, and_4_out);
  and and_13 (_4, C1, and_5_out);
  and and_14 (_5, C1, and_6_out);
  and and_15 (_6, C1, and_7_out);
  and and_16 (_7, C1, and_8_out);

  // Notes on the sheet:
  //   3:8 Decoder Flipped 
  //   Name: Carl Humphries
  //   Using Three inputs
  //   Student Number: S5084150
  //   The decoder turns it into one unique output
  //   Details on how it works are in the report.
  //   It is similar to representing an octal digit has been flipped for neatness in Part A 
endmodule

module Part_A (
  input  C1_3,
  input  C1_2,
  input  C1_1,
  input  C2_1,
  input  C2_2,
  input  C2_3,
  output Winner
);

  wire n3_8_decoder_0_top_7_bottom_1__0, n3_8_decoder_0_top_7_bottom_1__1, n3_8_decoder_0_top_7_bottom_1__2,
       n3_8_decoder_0_top_7_bottom_1__3, n3_8_decoder_0_top_7_bottom_1__4, n3_8_decoder_0_top_7_bottom_1__5,
       n3_8_decoder_0_top_7_bottom_1__6, n3_8_decoder_0_top_7_bottom_1__7, n3_8_decoder_7_top_0_bottom_1__0,
       n3_8_decoder_7_top_0_bottom_1__1, n3_8_decoder_7_top_0_bottom_1__2, n3_8_decoder_7_top_0_bottom_1__3,
       n3_8_decoder_7_top_0_bottom_1__4, n3_8_decoder_7_top_0_bottom_1__5, n3_8_decoder_7_top_0_bottom_1__6,
       n3_8_decoder_7_top_0_bottom_1__7;

  _3_8_Decoder_7_Top_0_Bottom u_3_8_decoder_7_top_0_bottom_1 (
    .C3(C1_3), .C2(C1_2), .C1(C1_1), ._7(n3_8_decoder_7_top_0_bottom_1__7),
    ._6(n3_8_decoder_7_top_0_bottom_1__6), ._5(n3_8_decoder_7_top_0_bottom_1__5),
    ._4(n3_8_decoder_7_top_0_bottom_1__4), ._3(n3_8_decoder_7_top_0_bottom_1__3),
    ._2(n3_8_decoder_7_top_0_bottom_1__2), ._1(n3_8_decoder_7_top_0_bottom_1__1),
    ._0(n3_8_decoder_7_top_0_bottom_1__0));
  _3_8_Decoder_0_Top_7_Bottom u_3_8_decoder_0_top_7_bottom_1 (
    .C1(C2_1), .C2(C2_2), .C3(C2_3), ._0(n3_8_decoder_0_top_7_bottom_1__0),
    ._1(n3_8_decoder_0_top_7_bottom_1__1), ._2(n3_8_decoder_0_top_7_bottom_1__2),
    ._3(n3_8_decoder_0_top_7_bottom_1__3), ._4(n3_8_decoder_0_top_7_bottom_1__4),
    ._5(n3_8_decoder_0_top_7_bottom_1__5), ._6(n3_8_decoder_0_top_7_bottom_1__6),
    ._7(n3_8_decoder_0_top_7_bottom_1__7));
  Card_Logic card_logic_1 (
    .C1_7(n3_8_decoder_7_top_0_bottom_1__7), .C1_6(n3_8_decoder_7_top_0_bottom_1__6),
    .C1_5(n3_8_decoder_7_top_0_bottom_1__5), .C1_4(n3_8_decoder_7_top_0_bottom_1__4),
    .C1_3(n3_8_decoder_7_top_0_bottom_1__3), .C1_2(n3_8_decoder_7_top_0_bottom_1__2),
    .C1_1(n3_8_decoder_7_top_0_bottom_1__1), .C1_0(n3_8_decoder_7_top_0_bottom_1__0),
    .C2_0(n3_8_decoder_0_top_7_bottom_1__0), .C2_1(n3_8_decoder_0_top_7_bottom_1__1),
    .C2_2(n3_8_decoder_0_top_7_bottom_1__2), .C2_3(n3_8_decoder_0_top_7_bottom_1__3),
    .C2_4(n3_8_decoder_0_top_7_bottom_1__4), .C2_5(n3_8_decoder_0_top_7_bottom_1__5),
    .C2_6(n3_8_decoder_0_top_7_bottom_1__6), .C2_7(n3_8_decoder_0_top_7_bottom_1__7), .C1_C2_7_True(Winner));

  // Notes on the sheet:
  //   Part_A
  //   Name: Carl Humphries
  //   Student Number: S5084150
  //   Decoders
  //   Details on how it works are in the report.
  //   Card Logic
  //   Using a combination of the card logic and the decoders it takes two card inputs and works out if they are >6
endmodule
